// Logisim project ALU.circ as structural Verilog: 1 circuit, main circuit ALU
module ALU (
  input  [31:0] A,
  input  [31:0] B,
  input  [4:0] Shift,
  input  CarryIn,
  input  [3:0] Codop,
  output [31:0] S,
  output [3:0] Flags
);

  wire C1, C2, C3, C4, N1;
  wire [31:0] ADC, AND_6156fd2f, ASR, BIC, bit_extender_1_out, bit_extender_2_out, bit_extender_3_out, CMN,
       CMP, EOR, LSL, LSR, MUL, MVN, not_1_out, ORR, ROR_edf90693, RSB, SBC, subtractor_2_out;

  assign AND_6156fd2f = A & B;  // AND_Gate and_1, 32 bits wide
  assign not_1_out = ~B;  // NOT_Gate not_1, 32 bits wide
  assign BIC = A & not_1_out;  // AND_Gate and_2, 32 bits wide
  assign ORR = A | B;  // OR_Gate or_1, 32 bits wide
  assign MVN = ~B;  // NOT_Gate not_2, 32 bits wide
  assign EOR = A ^ B;  // XOR_Gate xor_1, 32 bits wide
  Adder #(.width(32)) adder_1 (.a(A), .b(B), .out(ADC), .cin(CarryIn), .cout(C1));
  assign bit_extender_1_out = {{31{1'b0}}, 1'b0};  // Bit_Extender bit_extender_1
  Adder #(.width(32)) adder_2 (.a(A), .b(B), .out(CMN), .cin(1'b0), .cout(C4));
  Subtractor #(.width(32)) subtractor_1 (.a(bit_extender_1_out), .b(B), .out(RSB), .bin(1'b0));  // open: bout
  Shifter #(.width(32)) shifter_1 (.in(B), .\dist (Shift), .out(LSL));
  assign bit_extender_2_out = {{31{1'b0}}, 1'b0};  // Bit_Extender bit_extender_2
  Shifter #(.width(32), .shift("lr")) shifter_2 (.in(B), .\dist (Shift), .out(LSR));
  Subtractor #(.width(32)) subtractor_2 (.a(A), .b(B), .out(subtractor_2_out), .bin(1'b1), .bout(N1));
  Subtractor #(.width(32)) subtractor_3 (.a(A), .b(B), .out(CMP), .bin(1'b0), .bout(C3));
  Multiplier #(.width(32)) multiplier_1 (.a(A), .b(B), .out(MUL), .cin(bit_extender_2_out));  // open: cout
  Shifter #(.width(32), .shift("ar")) shifter_3 (.in(B), .\dist (Shift), .out(ASR));
  Adder #(.width(32)) adder_3 (.a(subtractor_2_out), .b(bit_extender_3_out), .out(SBC), .cin(1'b0), .cout(C2));
  assign bit_extender_3_out = {{31{1'b0}}, CarryIn};  // Bit_Extender bit_extender_3
  Multiplexer #(.select(4), .width(32), .enable("false")) multiplexer_1 (
    .in0(AND_6156fd2f), .in1(EOR), .in2(LSL), .in3(LSR), .in4(ASR), .in5(ADC), .in6(SBC), .in7(ROR_edf90693),
    .in8(AND_6156fd2f), .in9(RSB), .in10(CMP), .in11(CMN), .in12(ORR), .in13(MUL), .in14(BIC), .in15(MVN),
    .out({Flags[0], S[30:0]}), .sel(Codop));
  Shifter #(.width(32), .shift("rr")) shifter_4 (.in(B), .\dist (Shift), .out(ROR_edf90693));
  Multiplexer #(.select(4), .enable("false")) multiplexer_2 (
    .in0(1'b0), .in1(1'b0), .in2(1'b0), .in3(1'b0), .in4(1'b0), .in5(C1), .in6(C2), .in7(1'b0), .in8(1'b0),
    .in9(1'b0), .in10(C3), .in11(C4), .in12(1'b0), .in13(1'b0), .in14(1'b0), .in15(1'b0), .out(Flags[2]),
    .sel(Codop));
  Comparator #(.width(32)) comparator_1 (.a({32{1'b0}}), .b({Flags[0], S[30:0]}), .eq(Flags[1]));  // open: gt, lt

  assign S[31] = Flags[0];

  // Other names for the same wires on the sheet: Z = Flags[1]; C = Flags[2]; V = Flags[3]; N = Flags[0];
  //   TST[31:0] = AND_6156fd2f

  // Notes on the sheet:
  //   Note: for ROR, C = N
  //   Note 2: assume that shift > 0 for LSL and LSR
  //   Note: for ROR, C = N
endmodule
